// Logisim project new_CPU.circ as structural Verilog: 3 circuits, main circuit main
module main (
  input  [3:0] B,
  input  [3:0] A,
  input  [3:0] command
);

  ROM #(.dataWidth(12)) rom_1 (.data({command, A, B}));  // open: addr
  MyALU myalu_1 ();  // open: Cin, in_2, in_3, in_4, M, out_6, A_B, Sign
  ROM #(.addrWidth(4), .dataWidth(4)) rom_2 ();  // open: addr, data
endmodule

module MyALU (
  input  Cin,
  input  [3:0] in_2,
  input  [3:0] in_3,
  input  [3:0] in_4,
  input  M,
  output [3:0] out_6,
  output A_B,
  output Sign
);

  wire n74181_1_p13, n74181_1_p14, n74181_1_p16, n74181_1_p18, not_2_out;

  // _74181 74181_1: pin names not known; wires that end beside it: in_4[0], in_3[1], in_3[0], in_4[1], in_2[3], in_3[2], in_2[2], in_4[2], in_2[1], in_3[3], in_2[0], in_4[3], n74181_1_p13, n74181_1_p14, M, n74181_1_p16, out_6[0], n74181_1_p18, out_6[1], A_B, out_6[2], out_6[3]
  and and_1 (Sign, n74181_1_p14, not_2_out);
  not not_1 (n74181_1_p13, Cin);
  not not_2 (not_2_out, A_B);

  // Notes on the sheet:
  //   Op
  //   A_in
  //   B_in
  //   Output
  //   Cout
  //   Pn
endmodule

module Registers (
  output [3:0] out_1,
  output [3:0] A,
  output [3:0] out_3,
  output [3:0] out_4,
  output [3:0] out_5,
  output [3:0] out_6,
  output [3:0] out_7,
  output [3:0] out_8,
  output [3:0] out_9,
  output [3:0] B
);

  wire r0_w, r1_w, r2_w, r3_w, r4_w, r5_w, r6_w, r7_w, w;
  wire [2:0] A_t, B_t, t;
  wire [3:0] Data;

  Register #(.width(4)) r0 (.D(Data), .clk(r0_w));  // open: en, Q, clr
  Register #(.width(4)) r1 (.D(Data), .clk(r1_w));  // open: en, Q, clr
  Register #(.width(4)) r2 (.D(Data), .clk(r2_w));  // open: en, Q, clr
  Register #(.width(4)) r3 (.D(Data), .clk(r3_w));  // open: en, Q, clr
  Register #(.width(4)) r4 (.D(Data), .clk(r4_w));  // open: en, Q, clr
  Register #(.width(4)) r5 (.D(Data), .clk(r5_w));  // open: en, Q, clr
  Register #(.width(4)) r6 (.D(Data), .clk(r6_w));  // open: en, Q, clr
  Register #(.width(4)) r7 (.D(Data), .clk(r7_w));  // open: en, Q, clr
  Demultiplexer #(.select(3)) demultiplexer_1 (
    .out0(r0_w), .out1(r1_w), .out2(r2_w), .out3(r3_w), .out4(r4_w), .out5(r5_w), .out6(r6_w), .out7(r7_w),
    .in(w), .sel(t));
  Multiplexer #(.select(3), .width(4)) multiplexer_1 (
    .in0(out_1), .in1(out_3), .in2(out_4), .in3(out_5), .in4(out_6), .in5(out_7), .in6(out_8), .in7(out_9),
    .out(A), .sel(A_t));
  Multiplexer #(.select(3), .width(4)) multiplexer_2 (
    .in0(out_1), .in1(out_3), .in2(out_4), .in3(out_5), .in4(out_6), .in5(out_7), .in6(out_8), .in7(out_9),
    .out(B), .sel(B_t));

  // Other names for the same wires on the sheet: r0[3:0] = out_1; r1[3:0] = out_3; r2[3:0] = out_4; r3[3:0] = out_5;
  //   r4[3:0] = out_6; r5[3:0] = out_7; r6[3:0] = out_8; r7[3:0] = out_9
endmodule
